# Fritzing sketch SoDoKetNoiMach (saved by Fritzing 0.9.6b)

parts:
  M1 = Dagu DGServo 9g (Top view) [part_number=RS001B]
  S1 = Pushbutton [package="[SMD]"]
  Part1 = Arduino Uno (Rev3)
  R1 = Resistor [tolerance=±5% power=0.25 resistance=220 package=THT]
  SG1 = Buzzer 12mm [package=buzzer-ccv-kit]

nets:
  GND: M1.gnd, Part1.GND, R1.Pin_0, SG1.1
  VCC: M1.vcc, S1.Pin_3, S1.Pin_4, Part1.5V
  N1: M1.pulse, Part1.D9_PWM
  N2: S1.Pin_1, S1.Pin_2, Part1.D7, R1.Pin_1
  N3: Part1.D5_PWM, SG1.2
