# Fritzing sketch SoDoKetNoiMachPro (saved by Fritzing 0.9.6b)
breadboards: 1

parts:
  LCM1602_IIC2 = LCM1602 IIC [part_number="LCM1602 IIC" chip_label="LCM1602 IIC" package="DIP (Dual Inline) [THT]"]
  LCD2 = LCD screen
  Part1 = Arduino Uno (Rev3) - ICSP
  R1 = Resistor [tolerance=±5% resistance=220 package="0805 [SMD]"]
  LED1 = smd LED [color="Blue (505nm)" current=0.030 package="0603 [SMD]"]
  J3 = Buzzer
  SERVO1 = Tower Pro SG90 servo [part_number=101246]
  S1 = Pushbutton [package="[SMD]"]
  R2 = Resistor [tolerance=±5% resistance=220 package="0805 [SMD]"]

nets:
  VSS: LCM1602_IIC2.VSS, LCM1602_IIC2.VDD, LCM1602_IIC2.RS, LCM1602_IIC2.RW, LCM1602_IIC2.E, LCM1602_IIC2.D0, LCM1602_IIC2.D1, LCM1602_IIC2.D3, LCM1602_IIC2.D4, LCM1602_IIC2.D5, LCM1602_IIC2.D6, LCM1602_IIC2.D7, LCM1602_IIC2.K, LCD2.VSS, LCD2.VDD, LCD2.RS, LCD2.R/W, LCD2.E, LCD2.DB0, LCD2.DB1, LCD2.DB3, LCD2.DB4, LCD2.DB5, LCD2.DB6, LCD2.DB7, LCD2.LED-, J3.pin1
  N1: LCM1602_IIC2.V0, LCD2.V0
  N2: LCM1602_IIC2.D2, LCD2.DB2
  N3: LCM1602_IIC2.A, LCD2.LED+
  GND: LCM1602_IIC2.GND, Part1.GND, LED1.cathode, SERVO1.GND, R2.Pin_0
  VCC: LCM1602_IIC2.VCC, Part1.5V, SERVO1.+5V, S1.Pin_1, S1.Pin_2
  N4: LCM1602_IIC2.SDA, Part1.A4/SDA
  N5: LCM1602_IIC2.SCL, Part1.A5/SCL
  N6: Part1.D9_PWM, SERVO1.Signal
  N7: Part1.D11_PWM/MOSI, J3.pin2
  N8: Part1.D2, S1.Pin_3, S1.Pin_4, R2.Pin_1
  N9: Part1.D3_PWM, R1.Pin_1
  N10: R1.Pin_0, LED1.anode

custom parts:
  LCM1602 IIC: I2C-Module to use a 1602 or 2004 LCD on with the wire.h libory Serial LCD Modul
  Buzzer: Fixed frequency buzzer
  Tower Pro SG90 servo: Original file by John De Cristofaro http://www.adafruit.com/products/1449 Adafruit Feedback Servo (Small) Edited by: e-radionica.com 28/9/2015
